# Fritzing sketch IR-3LED (saved by Fritzing 0.9.3b)
breadboards: 1

parts:
  LED1 = LED - 5mm [color="Red (633nm)" package="5 mm [THT]"]
  LED2 = LED - 5mm [color="Red (633nm)" package="5 mm [THT]"]
  LED3 = LED - 5mm [color="Red (633nm)" package="5 mm [THT]"]
  IR1 = TSOP312.., 314.. [package=THT]
  R1 = Resistor [tolerance=±5% resistance=220 package="0805 [SMD]"]
  R2 = Resistor [tolerance=±5% resistance=220 package="0805 [SMD]"]
  R3 = Resistor [tolerance=±5% resistance=220 package="0805 [SMD]"]
  Part1 = Arduino Mega ADK (Rev3)

nets:
  GND: LED1.cathode, LED2.cathode, LED3.cathode, IR1.GND, Part1.GND
  N1: LED1.anode, R1.Pin_0
  N2: LED2.anode, R2.Pin_0
  N3: LED3.anode, R3.Pin_0
  5V: IR1.Vs, Part1.D8_PWM
  N4: IR1.Data, Part1.5V
  N5: R1.Pin_1, Part1.D7_PWM
  N6: R2.Pin_1, Part1.D6_PWM
  N7: R3.Pin_1, Part1.D5_PWM
