# Fritzing sketch ReactionGame (saved by Fritzing 0.9.3b)
breadboards: 1

parts:
  Part1 = Arduino Uno (Rev3)
  LED1 = smd LED [color="Blue (525nm)" package="1206 [SMD]"]
  R1 = Resistor [tolerance=±5% resistance=220 package=THT]
  S1 = Pushbutton [package="[SMD]"]
  LED2 = smd LED [color="Blue (525nm)" package="1206 [SMD]"]
  R2 = Resistor [tolerance=±5% resistance=220 package=THT]
  S2 = Pushbutton [package="[SMD]"]
  LED3 = smd LED [color="Red (633nm)" package="1206 [SMD]"]
  R3 = Resistor [tolerance=±5% resistance=220 package=THT]

nets:
  N1: Part1.D8, R1.Pin_1
  N2: Part1.D9_PWM, R2.Pin_0
  N3: Part1.D10_PWM/SS, R3.Pin_1
  GND: Part1.GND, LED1.cathode, S1.Pin_3, S1.Pin_4, LED2.cathode, S2.Pin_3, S2.Pin_4, LED3.cathode
  N4: Part1.D6_PWM, S1.Pin_1, S1.Pin_2
  N5: Part1.D7, S2.Pin_1, S2.Pin_2
  N6: LED1.anode, R1.Pin_0
  N7: LED2.anode, R2.Pin_1
  N8: LED3.anode, R3.Pin_0
