# Fritzing sketch SimpleCalculator (saved by Fritzing 0.9.3b)
breadboards: 1

parts:
  BUTTON = Pushbutton [package="[SMD]"]
  LED_RED_1 = smd LED [color="Red (633nm)" package="0603 [SMD]"]
  LED_RED_2 = smd LED [color="Red (633nm)" package="0603 [SMD]"]
  LED_BLUE_1 = smd LED [color="Blue (430nm)" package="0603 [SMD]"]
  U1 = 7-SEGMENT-4DIGIT [package=7-segment-4digit-youngsun]
  U2 = POT [package=pot_mammoth]
  R6 = Resistor [tolerance=±5% resistance=220 package=THT]
  R7 = Resistor [tolerance=±5% resistance=220 package=THT]
  R8 = Resistor [tolerance=±5% resistance=220 package=THT]
  R9 = Resistor [tolerance=±5% resistance=220 package=THT]
  R10 = Resistor [tolerance=±5% resistance=220 package=THT]
  R11 = Resistor [tolerance=±5% resistance=220 package=THT]
  Part2 = Arduino Mega ADK (Rev3)
  R5 = Resistor [tolerance=±5% resistance=220 package=THT]

nets:
  N1: BUTTON.Pin_1, BUTTON.Pin_2, Part2.D8_PWM
  GND: BUTTON.Pin_3, BUTTON.Pin_4, LED_RED_1.cathode, LED_RED_2.cathode, LED_BLUE_1.cathode, U2.S, Part2.GND
  LED_RED_DATA: LED_RED_1.anode, R5.Pin_0
  LED_BLUE_2_DATA: LED_RED_2.anode, R6.Pin_0
  LED_BLUE_1_DATA: LED_BLUE_1.anode, R7.Pin_0
  7SEG_1: U1.1, Part2.D35
  7SEG_2: U1.2, Part2.D37
  7SEG_3: U1.3, Part2.D39
  7SEG_4: U1.4, Part2.D41
  7SEG_5: U1.5, Part2.D43
  7SEG_6: U1.6, R8.Pin_0
  7SEG_7: U1.7
  7SEG_8: U1.8
  N2: U1.9, Part2.D23
  N3: U1.11, R11.Pin_1
  N4: U1.13, R10.Pin_1
  N5: U1.14, Part2.D29
  N6: U1.15, Part2.D31
  N7: U1.16, R9.Pin_1
  N8: U2.A, Part2.D9_PWM
  5V: U2.E, Part2.5V
  N9: R6.Pin_1, Part2.D6_PWM
  N10: R7.Pin_1, Part2.D5_PWM
  N11: R8.Pin_1, Part2.D45
  N12: R9.Pin_0, Part2.D33
  N13: R10.Pin_0, Part2.D27
  N14: R11.Pin_0, Part2.D25
  N15: Part2.D7_PWM, R5.Pin_1

// code stored in the sketch: SimpleCalculator.ino
private int LED_RED_1_PIN = 7;
private int LED_RED_2_PIN = 6;
private int LED_BLUE_1_PIN = 5;


void setup() {
	Serial.begin(9600);
	
	pinMode(LED_RED_1_PIN, OUTPUT);
	pinMode(LED_RED_2_PIN, OUTPUT);
	pinMode(LED_BLUE_1_PIN, OUTPUT);

	digitalWrite(LED_BLUE_1_PIN, 255);
	digitalWrite(LED_RED_1_PIN, 255);
	digitalWrite(LED_RED_2_PIN, 255);
}

void loop() {

}
