# Fritzing sketch SimpleCalculatorEnhanced (saved by Fritzing 0.9.3b)
breadboards: 1

parts:
  BUTTON = Pushbutton [package="[SMD]"]
  LED_RED_1 = smd LED [color="Red (633nm)" package="0603 [SMD]"]
  LED_RED_2 = smd LED [color="Red (633nm)" package="0603 [SMD]"]
  LED_BLUE_1 = smd LED [color="Blue (430nm)" package="0603 [SMD]"]
  U2 = POT [package=pot_mammoth]
  R6 = Resistor [tolerance=±5% resistance=220 package=THT]
  R7 = Resistor [tolerance=±5% resistance=220 package=THT]
  R8 = Resistor [tolerance=±5% resistance=220 package=THT]
  R9 = Resistor [tolerance=±5% resistance=220 package=THT]
  R10 = Resistor [tolerance=±5% resistance=220 package=THT]
  R11 = Resistor [tolerance=±5% resistance=220 package=THT]
  Part2 = Arduino Mega ADK (Rev3)
  R5 = Resistor [tolerance=±5% resistance=220 package=THT]
  BUTTON1 = Pushbutton [package="[SMD]"]
  U1 = 7-SEGMENT-4DIGIT [package=7-segment-4digit-youngsun]

nets:
  N1: BUTTON.Pin_1, BUTTON.Pin_2, Part2.D8_PWM
  GND: BUTTON.Pin_3, BUTTON.Pin_4, LED_RED_1.cathode, LED_RED_2.cathode, LED_BLUE_1.cathode, U2.S, Part2.GND, BUTTON1.Pin_3, BUTTON1.Pin_4
  LED_RED_DATA: LED_RED_1.anode, R5.Pin_0
  LED_BLUE_2_DATA: LED_RED_2.anode, R6.Pin_0
  LED_BLUE_1_DATA: LED_BLUE_1.anode, R7.Pin_0
  N2: U2.A, Part2.A0
  5V: U2.E, Part2.5V
  N3: R6.Pin_1, Part2.D6_PWM
  N4: R7.Pin_1, Part2.D5_PWM
  7SEG_6: R8.Pin_0, U1.6
  N5: R8.Pin_1, Part2.D45
  N6: R9.Pin_0, Part2.D33
  N7: R9.Pin_1, U1.16
  N8: R10.Pin_0, Part2.D27
  N9: R10.Pin_1, U1.13
  N10: R11.Pin_0, Part2.D25
  N11: R11.Pin_1, U1.11
  N12: Part2.D9_PWM, BUTTON1.Pin_1, BUTTON1.Pin_2
  N13: Part2.D7_PWM, R5.Pin_1
  N14: Part2.D23, U1.9
  N15: Part2.D29, U1.14
  N16: Part2.D31, U1.15
  7SEG_1: Part2.D35, U1.1
  7SEG_2: Part2.D37, U1.2
  7SEG_3: Part2.D39, U1.3
  7SEG_4: Part2.D41, U1.4
  7SEG_5: Part2.D43, U1.5
  7SEG_7: U1.7
  7SEG_8: U1.8

// code stored in the sketch: SimpleCalculator.ino
private int LED_RED_1_PIN = 7;
private int LED_RED_2_PIN = 6;
private int LED_BLUE_1_PIN = 5;


void setup() {
	Serial.begin(9600);
	
	pinMode(LED_RED_1_PIN, OUTPUT);
	pinMode(LED_RED_2_PIN, OUTPUT);
	pinMode(LED_BLUE_1_PIN, OUTPUT);

	digitalWrite(LED_BLUE_1_PIN, 255);
	digitalWrite(LED_RED_1_PIN, 255);
	digitalWrite(LED_RED_2_PIN, 255);
}

void loop() {

}
